# Fritzing sketch one-key-keyboard (saved by Fritzing 0.9.5d)
breadboards: 1

parts:
  Part12 = Arduino Pro Micro (Clone)
  S1 = Momentary Switch [package=ksa_sealed_tac_switch]
  LED1 = LED - 3mm [color="Red (633nm)" package="3 mm [THT]"]
  R1 = Resistor [tolerance=±5% resistance=220 package="0603 [SMD]"]

nets:
  N1: Part12.GND, S1.1, S1.2, LED1.cathode, R1.Pin_1
  N2: Part12.D6, R1.Pin_0
  N3: Part12.D9, S1.3, S1.4
